# Fritzing sketch Q10 (saved by Fritzing 0.9.4)
breadboards: 1

parts:
  U1 = NodeMCU V1.0
  LED1 = smd LED [color="Red (633nm)" package="1206 [SMD]"]
  R1 = Photocell (LDR) [package=THT]
  R2 = Resistor [tolerance=±10% resistance=10k package="0805 [SMD]"]
  R3 = Resistor [tolerance=±10% resistance=330 package="0805 [SMD]"]

nets:
  N1: U1.D1, LED1.anode
  N2: U1.GND, R1.pin_0, R3.Pin_0
  N3: U1.Vin, R2.Pin_1
  N4: U1.A0, R1.pin_1, R2.Pin_0
  N5: LED1.cathode, R3.Pin_1

custom parts:
  NodeMCU V1.0: ESP8266 based NodeMCU
