# Fritzing sketch Q8_P2 (saved by Fritzing 0.9.4)
breadboards: 1

parts:
  U1 = NodeMCU V1.0
  LED1 = smd LED [color="Red (633nm)" package="1206 [SMD]"]
  R1 = Photocell (LDR) [package=THT]
  R2 = Resistor [tolerance=±10% resistance=10k package="0805 [SMD]"]
  R3 = Resistor [tolerance=±10% resistance=330 package="0805 [SMD]"]
  LED2 = LED - 5mm [color="Red (633nm)" package="5 mm [THT]"]
  R4 = Resistor [tolerance=±10% resistance=330 package="0805 [SMD]"]
  Mod1 = KY-012 Active Buzzer Module [package="Breakout board"]

nets:
  N1: U1.D0, Mod1.NC
  N2: U1.D1, LED2.anode
  N3: U1.3V3, LED1.anode, R1.pin_0, Mod1.S
  N4: U1.GND, R2.Pin_0, R3.Pin_0, R4.Pin_0, Mod1.-
  N5: U1.A0, R1.pin_1, R2.Pin_1
  N6: LED1.cathode, R3.Pin_1
  N7: LED2.cathode, R4.Pin_1

custom parts:
  NodeMCU V1.0: ESP8266 based NodeMCU
  KY-012 Active Buzzer Module: Active Piezoelectric Buzzer Module KY-012, it produces single-tone sound when signal is high. (Special thanks to vanepp for fixing the PCB holes and other errors)
