# Fritzing sketch Q8_P3 (saved by Fritzing 0.9.4)
breadboards: 1

parts:
  J1 = Basic Servo  # not connected
  U3 = NodeMCU V1.0
  R1 = Resistor [tolerance=±5% resistance=220 package=THT]
  LED1 = LED - 5mm [color="Red (633nm)" package="5 mm [THT]"]
  LED2 = LED - 5mm [color="Red (633nm)" package="5 mm [THT]"]
  R2 = Resistor [tolerance=±5% resistance=220 package=THT]
  R3 = Resistor [tolerance=±5% resistance=220 package=THT]
  LED3 = LED - 5mm [color="Red (633nm)" package="5 mm [THT]"]
  R4 = Photocell (LDR) [package=THT]
  R5 = Photocell (LDR) [package=THT]
  R6 = Photocell (LDR) [package=THT]
  R8 = Resistor [tolerance=±10% resistance=10k package="0805 [SMD]"]
  R9 = Resistor [tolerance=±10% resistance=10k package="0805 [SMD]"]
  R10 = Resistor [tolerance=±10% resistance=10k package="0805 [SMD]"]

nets:
  N1: U3.D0, R6.pin_0, R8.Pin_1
  N2: U3.D1, R5.pin_0, R9.Pin_1
  N3: U3.D2, R4.pin_0, R10.Pin_1
  N4: U3.3V3, LED1.anode, LED2.anode, LED3.anode, R6.pin_1
  N5: U3.GND, R3.Pin_0, R8.Pin_0, R9.Pin_0, R10.Pin_0
  N6: R1.Pin_1, LED1.cathode
  N7: LED2.cathode, R2.Pin_1
  N8: R3.Pin_1, LED3.cathode

custom parts:
  NodeMCU V1.0: ESP8266 based NodeMCU
