# Fritzing sketch Q9 (saved by Fritzing 0.9.4)
breadboards: 1

parts:
  Part1 = SRF05 Ultrasonic Rangefinder
  J1 = Basic Servo  # not connected
  U3 = NodeMCU V1.0

nets:
  VCC: Part1.VCC, U3.D4, U3.3V3
  N1: Part1.Trig, U3.D0
  N2: Part1.Echo, U3.D1, U3.D2
  GND: Part1.GND, U3.GND, U3.D5

custom parts:
  NodeMCU V1.0: ESP8266 based NodeMCU
